# Fritzing sketch Motion Detector Camera (saved by Fritzing 0.9.2b)
breadboards: 1

parts:
  U1 = mystery part, 8 pins [chip_label="ePIR zDOT SBC"]
  Pi1 = Adafruit Pi Cobbler
  R1 = Resistor [tolerance=±5% resistance=330 package="0805 [SMD]"]
  LED1 = smd LED [color="Red (633nm)" package="0603 [SMD]"]
  R2 = Resistor [tolerance=±5% resistance=330 package="0805 [SMD]"]
  R4 = Resistor [tolerance=±5% resistance=330 power=3W package=THT]
  R5 = Resistor [tolerance=±5% resistance=330 power=3W package=THT]
  R6 = Resistor [tolerance=±5% resistance=330 power=3W package=THT]
  R7 = Resistor [tolerance=±5% resistance=330 power=3W package=THT]
  LED2 = RGB LED (com. cathode, rgb) [package="5 mm [THT]"]

nets:
  N1: U1.pin1, U1.pin8, Pi1.GND, Pi1.PIN20, R2.Pin_1, R5.Pin_0
  N2: U1.pin2, U1.pin6, Pi1.5V0, R1.Pin_0
  N3: U1.pin3, Pi1.TXD
  N4: U1.pin4, Pi1.RXD, R1.Pin_1
  N5: U1.pin5, Pi1.#22
  N6: U1.pin7, Pi1.#23
  N7: Pi1.#17, LED1.anode
  N8: Pi1.MOSI, R7.Pin_0
  N9: Pi1.MISO, R6.Pin_0
  N10: Pi1.CE0, R4.Pin_0
  N11: LED1.cathode, R2.Pin_0
  N12: R4.Pin_1, LED2.blue_anode
  N13: R5.Pin_1, LED2.common_cathode
  N14: R6.Pin_1, LED2.green_anode
  N15: R7.Pin_1, LED2.red_anode

custom parts:
  Adafruit Pi Cobbler: Adafruit Pi Cobbler GPIO Breakout for Raspberry Pi

// code stored in the sketch: Motion Detector Camera.ino
#!/usr/bin/python
import RPi.GPIO as GPIO
import time
import serial
import sys

GPIO.setwarnings(False) # Disable "this channel already in use", etc.

# Constants 
ACK =  6 # "Acknowledge" character
NACK = 21 # "Non-Acknowledge" character
LEDPIN = 11	# Status - could do without
MDPIN = 15	# Motion Detected pin

def readLineCR(port):
	s = ''
	while	True:
		try:
			ch = port.read()
			s += ch
			if ch == '\r' or ch == '':
				break
		except:
			pass # Will be a "ready to read, but no data", in my experience.
	return s

def main(argc, argv):
	print "Initializing... "
	GPIO.setmode(GPIO.BOARD)
	#time.sleep(5) # Wait 5 seconds before communicating with ePir zDot

	port = serial.Serial("/dev/ttyAMA0", baudrate = 9600, timeout = 2)

	#time.sleep(10) # Arduino example says need delays between commands for proper operation. (I suspect for 9600 bps it needs time.)
	time.sleep(1)
	ch = 'U'
	while ch == 'U': # Repeat loop if not stablized. (ePIR replies with the character 'U' until the device becomes stable) 
	  time.sleep(1)
	  ch = port.read(1) # Sends status command to ePIR and assigns reply from ePIR to variable ch. (READ ONLY function)
	  print 'ch = %s' % (ch, )
  
	#ch = readLine(port)
	print "ch = '%s'\r\nDevice Ready" % (ch, )
	time.sleep(1)
	
	port.write('CM');
	result = readLineCR(port)
	if result == 'R':
		print 'ePIR reset!'
	elif result == 'M':
		print 'Motion detection mode confirmed.'
	else:
		print 'Result = "%s"' % (result, )
	
	GPIO.setup(LEDPIN, GPIO.OUT) # Light (blink?) when motion detected
	GPIO.setup(MDPIN, GPIO.IN)
	
	print "Running..."
	while True:
	  motionDetected = GPIO.input(MDPIN)
	  print '\rmotionDetected = %d' % (motionDetected, ) ,
	  if motionDetected == 0:
			print '\nMotion detected!'
			for j in range(0,10):
				GPIO.output(LEDPIN, True)
				time.sleep(0.05)
				GPIO.output(LEDPIN, False)
				time.sleep(0.05)
			GPIO.output(LEDPIN, True)
			GPIO.output(LEDPIN, False)
			time.sleep(2)
	port.close()

if __name__ == "__main__":
	main(len(sys.argv), sys.argv)

// code stored in the sketch: Motion Detector.fzz.ino
#!/usr/bin/python
# This script is a straight motion detector.
# Author: Leland Green... (aboogieman at gmail dot com)
import RPi.GPIO as GPIO
import time
import serial
import sys

GPIO.setwarnings(False) # Disable "this channel already in use", etc.

# Constants 
ACK =  6 # "Acknowledge" character
NACK = 21 # "Non-Acknowledge" character
LEDPIN = 11	# Status - could do without
MDPIN = 15	# Motion Detected pin

def readLineCR(port):
	s = ''
	while	True:
		try:
			ch = port.read()
			s += ch
			if ch == '\r' or ch == '':
				break
		except:
			pass # Will be a "ready to read, but no data", in my experience.
	return s

def main(argc, argv):
	print "Initializing... "
	GPIO.setmode(GPIO.BOARD)
	#time.sleep(5) # Wait 5 seconds before communicating with ePir zDot

	port = serial.Serial("/dev/ttyAMA0", baudrate = 9600, timeout = 2)

	#time.sleep(10) # Arduino example says need delays between commands for proper operation. (I suspect for 9600 bps it needs time.)
	time.sleep(1)
	ch = 'U'
	while ch == 'U': # Repeat loop if not stablized. (ePIR replies with the character 'U' until the device becomes stable) 
	  time.sleep(1)
	  ch = port.read(1) # Sends status command to ePIR and assigns reply from ePIR to variable ch. (READ ONLY function)
	  print 'ch = %s' % (ch, )
  
	#ch = readLine(port)
	print "ch = '%s'\r\nDevice Ready" % (ch, )
	#time.sleep(10)
	time.sleep(1)
	
	port.write('CM');
	result = readLineCR(port)
	if result == 'R':
		print 'ePIR reset!'
	elif result == 'M':
		print 'Motion detection mode confirmed.'
	else:
		print 'Result = "%s"' % (result, )
	
	GPIO.setup(LEDPIN, GPIO.OUT) # Light (blink?) when motion detected
	GPIO.setup(MDPIN, GPIO.IN)
	
	print "Running..."
	while True:
	  motionDetected = GPIO.input(MDPIN)
	  print '\rmotionDetected = %d' % (motionDetected, ) ,
	  if motionDetected == 0:
			print '\nMotion detected!'
			for j in range(0,10):
				GPIO.output(LEDPIN, True)
				time.sleep(0.05)
				GPIO.output(LEDPIN, False)
				time.sleep(0.05)
			GPIO.output(LEDPIN, True)
			GPIO.output(LEDPIN, False)
			time.sleep(1)
	port.close()

if __name__ == "__main__":
	main(len(sys.argv), sys.argv)

// code stored in the sketch: Motion Detector.ino
#!/usr/bin/python
#Small example scripti by Leland Green... 20160205 Copyright (c) All Rights Reserved except:
# You may freely modify and disctribute the code as long as you attribute the original to me.
# (MIT License.)
import RPi.GPIO as GPIO
import time
import serial
import sys

GPIO.setwarnings(False) # Disable "this channel already in use", etc.

# Constants
ACK =  6 # "Acknowledge" character
NACK = 21 # "Non-Acknowledge" character
LEDPIN = 11    # Status - could do without
MDPIN = 15 # Motion Detected pin

def readLineCR(port):
   s = ''
   while  True:
      try:
         ch = port.read(1)
         s += ch
         if ch == '\r' or ch == '':
            break
      except:
         pass # Will be a "ready to read, but no data", in my experience.
   return s

def main(argc, argv):
   print "Initializing... "
   GPIO.setmode(GPIO.BOARD)
   #time.sleep(5) # Wait 5 seconds before communicating with ePir zDot

   port = serial.Serial("/dev/ttyAMA0", baudrate = 9600, timeout = 2)

   time.sleep(10) # Arduino example says need delays between commands for proper operation. (I suspect for 9600 bps it needs time.)
   #time.sleep(1)
   ch = 'U'
   while ch == 'U': # Repeat loop if not stablized. (ePIR replies with the character 'U' until the device becomes stable) 
     #time.sleep(1)
     ch = port.read(1) # Sends status command to ePIR and assigns reply from ePIR to variable ch. (READ ONLY function)
     print 'ch = %s' % (ch, )
  
   ch = readLineCR(port)
   #time.sleep(10)
   time.sleep(1)
   print "ePIR Device Ready"
   
   port.write('CM')
   time.sleep(1)
   result = readLineCR(port)
   if result == 'R':
      print 'ePIR reset!'
   elif result == 'M':
      print 'Motion detection mode confirmed.'
   else:
      print 'Result = "%s"' % (result, )
   
   GPIO.setup(LEDPIN, GPIO.OUT) # Light (blink?) when motion detected
   GPIO.setup(MDPIN, GPIO.IN)
   
   print "Running..."
   while True:
     motionDetected = GPIO.input(MDPIN)
     print '\rmotionDetected = %d' % (motionDetected, ) ,
     if motionDetected == 0:
         print '\nMotion detected!'
         for j in range(0,10):
            GPIO.output(LEDPIN, True)
            time.sleep(0.05)
            GPIO.output(LEDPIN, False)
            time.sleep(0.05)
         GPIO.output(LEDPIN, True)
         GPIO.output(LEDPIN, False)
         time.sleep(1)
   port.close()
   GPIO.cleanup()

if __name__ == "__main__":
   main(len(sys.argv), sys.argv)

// code stored in the sketch: Security Camera.ino
#!/usr/bin/python
	import RPi.GPIO as GPIO
import time
import serial
import sys

GPIO.setwarnings(False) # Disable "this channel already in use", etc.

# Constants
ACK =  6 # "Acknowledge" character
NACK = 21 # "Non-Acknowledge" character
LEDPIN = 11    # Status - could do without
MDPIN = 15 # Motion Detected pin

def readLineCR(port):
   s = ''
   while  True:
      try:
         ch = port.read(1)
         s += ch
         if ch == '\r' or ch == '':
            break
      except:
         pass # Will be a "ready to read, but no data", in my experience.
   return s

def main(argc, argv):
   print "Initializing... "
   GPIO.setmode(GPIO.BOARD)
   #time.sleep(5) # Wait 5 seconds before communicating with ePir zDot

   port = serial.Serial("/dev/ttyAMA0", baudrate = 9600, timeout = 2)

   time.sleep(10) # Arduino example says need delays between commands for proper operation. (I suspect for 9600 bps it needs time.)
   #time.sleep(1)
   ch = 'U'
   while ch == 'U': # Repeat loop if not stablized. (ePIR replies with the character 'U' until the device becomes stable) 
     #time.sleep(1)
     ch = port.read(1) # Sends status command to ePIR and assigns reply from ePIR to variable ch. (READ ONLY function)
     print 'ch = %s' % (ch, )
  
   ch = readLineCR(port)
   #time.sleep(10)
   time.sleep(1)
   print "ePIR Device Ready"
   
   port.write('CM')
   time.sleep(1)
   result = readLineCR(port)
   if result == 'R':
      print 'ePIR reset!'
   elif result == 'M':
      print 'Motion detection mode confirmed.'
   else:
      print 'Result = "%s"' % (result, )
   
   GPIO.setup(LEDPIN, GPIO.OUT) # Light (blink?) when motion detected
   GPIO.setup(MDPIN, GPIO.IN)
   
   print "Running..."
   while True:
     motionDetected = GPIO.input(MDPIN)
     print '\rmotionDetected = %d' % (motionDetected, ) ,
     if motionDetected == 0:
         print '\nMotion detected!'
         for j in range(0,10):
            GPIO.output(LEDPIN, True)
            time.sleep(0.05)
            GPIO.output(LEDPIN, False)
            time.sleep(0.05)
         GPIO.output(LEDPIN, True)
         GPIO.output(LEDPIN, False)
         time.sleep(1)
   port.close()
   GPIO.cleanup()

if __name__ == "__main__":
   main(len(sys.argv), sys.argv)

// code stored in the sketch: Security Camera.py.ino
#!/usr/bin/python
# Based on the "security camera" example Python script found on Linphone.org here:
# Heavily modified to add motion detector features for Zilog ePIR SBC with ZDots. This is an advanced
# version and I cannot find this exact model, so I think it's discontinued. Should work with minor 
# modifications (and removal of features?) on other motion detectors.
#
# Please let me know if you have questions!
# Modifications by: Leland Green - aboogieman@gmail.com

import datetime
from email.MIMEMultipart import MIMEMultipart
from email.MIMEText import MIMEText
from email.MIMEImage import MIMEImage
import RPi.GPIO as GPIO
import io
import linphone
import logging
import picamera
import serial
import signal
import time
import smtplib
import sys

# Constants 
emailFromAddress = 'lelandgreenlabs'
emailAddressTo = 'aboogieman@gmail.com'
emailSubject = 'Motion detected'
emailTextAlternate = 'Motion was detected. An image is included in the other MIME part of this email.'

detectMotion = True  # Whether or not we have the motion detector SBC connected. True = connected.
ACK =  6 # "Acknowledge" character
NACK = 21 # "Non-Acknowledge" character
LEDPIN = 11  # Status - could do without
MDPIN = 15  # Motion Detected pin

WAITSECONDS = 20  # Set to zero to send a message every time motion is detected.
									# WAITSECONDS also controls the shortest amount of time between printing "Motiono detected".
WAITEMAILSECONDS = 30

def readLineCR(port):
  s = ''
  while  True:
    try:
      ch = port.read()
      s += ch
      if ch == '\r' or ch == '':
        break
    except: # TODO: Add specific exceptions here.
      pass # Will be a "ready to read, but no data", in my experience.
  return s
 
class SecurityCamera:
  def __init__(self, username='', password='', whitelist=[], camera='', snd_capture='', snd_playback=''):
    self.quit = False
    self.whitelist = whitelist
    callbacks = {
      'call_state_changed': self.call_state_changed,
    }
    print "__init__"
    
    # Configure the linphone core
    logging.basicConfig(level=logging.INFO)
    signal.signal(signal.SIGINT, self.signal_handler)
    print "calling set_log_handler()"
    linphone.set_log_handler(self.log_handler)
    print "calling linphone.Core.new(...)"
    self.core = linphone.Core.new(callbacks, None, None)
    self.core.max_calls = 1
    self.core.echo_cancellation_enabled = True
    self.core.video_capture_enabled = True
    self.core.video_display_enabled = False
    print "Setting stun server"
    self.core.stun_server = 'stun.linphone.org'
    self.core.firewall_policy = linphone.FirewallPolicy.PolicyUseIce
    if len(camera):
      self.core.video_device = camera
    if len(snd_capture):
      self.core.capture_device = snd_capture
    if len(snd_playback):
      self.core.playback_device = snd_playback
    
    # Only enable PCMU and PCMA audio codecs
    for codec in self.core.audio_codecs:
      if codec.mime_type == "PCMA" or codec.mime_type == "PCMU":
        self.core.enable_payload_type(codec, True)
      else:
        self.core.enable_payload_type(codec, False)
    
    print "setting audio_dscp"
    # Pulling my values from "Commonly used DSCP Values" table in this article: 
    # https://en.wikipedia.org/wiki/Differentiated_services
    self.core.audio_dscp = 46 # 46 = High Priority Expedited Forwarding (EF) - TODO: Can this be lowered???
    
    # Only enable VP8 video codec
    for codec in self.core.video_codecs:
      if codec.mime_type == "VP8":
        self.core.enable_payload_type(codec, True)
      else:
        self.core.enable_payload_type(codec, False)
    
    self.configure_sip_account(username, password)
    
    #Initialize the motion detector. This is for the Zilog ePIR ZDot SBC. It has more features via serial mode,
    # so that's what we'll use here. 
    GPIO.setwarnings(False) # Disable "this channel already in use", etc.    
    
    GPIO.setmode(GPIO.BOARD)
    self.port = serial.Serial("/dev/ttyAMA0", baudrate = 9600, timeout = 2)
    
    #time.sleep(10) # Arduino example says need delays between commands for proper operation. (I suspect for 9600 bps it needs time.)
    time.sleep(1)
    ch = 'U'
    while ch == 'U': # Repeat loop if not stablized. (ePIR replies with the character 'U' until the device becomes stable) 
      time.sleep(1)
      ch = self.port.read(1) # Sends status command to ePIR and assigns reply from ePIR to variable ch. (READ ONLY function)
      print 'ch = %s' % (ch, )
      
    #ch = readLine(self.port)
    print "ch = '%s'\r\nDevice Ready" % (ch, )
    time.sleep(1)
    
    self.port.write('CM');
    result = readLineCR(self.port)
    if result == 'R':
      print 'ePIR reset!'
    elif result == 'M':
      print 'Motion detection mode confirmed.'
    else:
      print 'Result = "%s"' % (result, )
    
    GPIO.setup(LEDPIN, GPIO.OUT) # Light (blink?) when motion detected
    GPIO.setup(MDPIN, GPIO.IN)

    self.smtp = smtplib.SMTP()
    self.smtp.connect('smtp.gmail.com', 587)
    
    self.camera = picamera.PiCamera()
    self.lastMessageTicks = time.time()
    self.lastEmailTicks = time.time()
    self.imgStream = io.BytesIO()
    self.configured = False
  
  def captureImage(self):
    # Create an in-memory stream
    self.camera.start_preview()
    # Camera warm-up time
    time.sleep(2)
    fname = '%s' + str(datetime.datetime.now())
    self.camera.capture(self.imgStream, 'jpeg')
    self.camera.stop_preview()
    return self.imgStream
  
  def emailImage(self):
    self.captureImage()
    
    # Create the root message and fill in the from, to, and subject headers
    msgRoot = MIMEMultipart('related')
    msgRoot['Subject'] = 'Motion detected'
    msgRoot['From'] = emailFromAddress
    msgRoot['To'] = emailAddressTo
    msgRoot.preamble = 'This is a multi-part message in MIME format.'
    
    # Encapsulate the plain and HTML versions of the message body in an
    # 'alternative' part, so message agents can decide which they want to display.
    msgAlternative = MIMEMultipart('alternative')
    msgRoot.attach(msgAlternative)
    
    msgText = MIMEText(emailTextAlternate)
    msgAlternative.attach(msgText)
    
    # We reference the image in the IMG SRC attribute by the ID we give it below
    msgText = MIMEText('<b>Some <i>HTML</i> text</b> and an image.<br><img src="cid:image1"><br>Nifty!', 'html')
    msgAlternative.attach(msgText)
    
    # This example assumes the image is in the current directory
    self.imgStream.seek(0)
    msgImage = MIMEImage(self.imgStream.read())
    
    # Define the image's ID as referenced above
    msgImage.add_header('Content-ID', '<image1>')
    msgRoot.attach(msgImage)
    
    # Send the email (this example assumes SMTP authentication is required)
    self.smtp.starttls()
    self.smtp.login('lelandgreenlabs@gmail.com', 'amd7VHXUnZXd')
    self.smtp.sendmail(emailFromAddress, emailAddressTo, msgRoot.as_string())
    self.smtp.quit()
    self.lastEmailTicks = time.time()
  
  def signal_handler(self, signal, frame):
    self.core.terminate_all_calls()
    self.quit = True
  
  def log_handler(self, level, msg):
    method = getattr(logging, level)
    method(msg)
  
  def call_state_changed(self, core, call, state, message):
    if state == linphone.CallState.IncomingReceived:
      if call.remote_address.as_string_uri_only() in self.whitelist:
        params = core.create_call_params(call)
        core.accept_call_with_params(call, params)
      else:
        core.decline_call(call, linphone.Reason.Declined)
        for contact in self.whitelist:
          chat_room = core.get_chat_room_from_uri(contact)
          if not chat_room:
            continue
          msg = chat_room.create_message(call.remote_address_as_string + ' tried to call')
          chat_room.send_chat_message(msg)
  
  def configure_sip_account(self, username, password):
    # Configure the SIP account
    proxy_cfg = self.core.create_proxy_config()
    proxy_cfg.identity_address = self.core.create_address('sip:{username}@sip.linphone.org'.format(username=username))
    proxy_cfg.server_addr = 'sip:sip.linphone.org;transport=tls'
    proxy_cfg.register_enabled = True
    self.core.add_proxy_config(proxy_cfg)
    auth_info = self.core.create_auth_info(username, None, password, None, None, 'sip.linphone.org')
    self.core.add_auth_info(auth_info)
  
  def run(self):
		while not self.quit:
		  self.core.iterate()
		  if detectMotion:
		    # Incoming calls have been handled, so check the motion detector:
		    motionDetected = GPIO.input(MDPIN)
		    #print '\rmotionDetected = %d' % (motionDetected, ) ,
		    if motionDetected == 0:
		      if time.time() - self.lastMessageTicks > WAITSECONDS:
		        for contact in self.whitelist:
		          chat_room = self.core.get_chat_room_from_uri(contact)
		          if not chat_room:
		            continue
		          dt = datetime.datetime.now()
		          msg = chat_room.create_message('Motion detected on camera at %s' % (dt.isoformat(' ')))
		          chat_room.send_chat_message(msg)
		          self.lastMessageTicks = time.time()
		        print '\nMotion detected!'
		        for j in range(0,10):
		          GPIO.output(LEDPIN, True)
		          time.sleep(0.05)
		          GPIO.output(LEDPIN, False)
		          time.sleep(0.05)
		        GPIO.output(LEDPIN, True)
		        GPIO.output(LEDPIN, False)
		      # Note that times for message and email are independent.
		      if time.time() - self.lastEmailTicks > WAITEMAILSECONDS:
		        self.lastEmailTicks = time.time()
		        self.emailImage()
		  else:
		    time.sleep(0.01) # time.sleep(0.03)

def main(argc, argv):
  cam = SecurityCamera(username='lelandgreen', password='wMYV16RFGodt', whitelist=['sip:lelandgreen@sip.linphone.org'], camera='V4L2: /dev/video0', snd_capture='ALSA: Set [C-Media USB Headphone Set]', snd_playback='ALSA: USB Audio [USB Audio]')
  cam.run()

if __name__ == '__main__':
	main(len(sys.argv), sys.argv)
